// Logisim project TallerLogica-Combinatorios.circ as structural Verilog: 10 circuits, main circuit sumador_simple
module sumador_simple (
  input  a,
  input  b,
  output S,
  output Cout
);

  xor xor_1 (S, a, b);
  and and_1 (Cout, a, b);
endmodule

module sumador_completo (
  input  Cin,
  input  A,
  input  B,
  output S,
  output Cout
);

  wire and_1_out, and_2_out, and_3_out, and_4_out, xor_1_out;

  ExactlyOne xor_1 (.out(xor_1_out), .in1(Cin), .in2(A), .in3(B));
  and and_1 (and_1_out, Cin, A, B);
  and and_2 (and_2_out, Cin, A);
  and and_3 (and_3_out, Cin, B);
  and and_4 (and_4_out, A, B);
  or or_1 (S, xor_1_out, and_1_out);
  or or_2 (Cout, and_1_out, and_2_out, and_3_out, and_4_out);
endmodule

module sumador_4 (
  input  Cin,
  input  [3:0] A,
  input  [3:0] B,
  output [3:0] S,
  output Cout
);

  wire and_1_out, and_2_out, and_3_out, and_4_out, and_5_out, and_6_out, and_7_out, and_8_out, and_9_out,
       and_10_out, and_11_out, and_12_out, and_13_out, and_14_out, and_15_out, and_16_out, or_3_out,
       or_4_out, or_8_out, xor_1_out, xor_2_out, xor_3_out, xor_4_out;

  ExactlyOne xor_1 (.out(xor_1_out), .in1(or_8_out), .in2(A[2]), .in3(B[2]));
  and and_1 (and_1_out, or_8_out, A[2], B[2]);
  and and_2 (and_2_out, or_8_out, A[2]);
  and and_3 (and_3_out, or_8_out, B[2]);
  and and_4 (and_4_out, A[2], B[2]);
  ExactlyOne xor_2 (.out(xor_2_out), .in1(Cin), .in2(A[0]), .in3(B[0]));
  and and_5 (and_5_out, Cin, A[0], B[0]);
  and and_6 (and_6_out, Cin, A[0]);
  and and_7 (and_7_out, Cin, B[0]);
  and and_8 (and_8_out, A[0], B[0]);
  or or_1 (S[2], xor_1_out, and_1_out);
  or or_2 (S[0], xor_2_out, and_5_out);
  or or_3 (or_3_out, and_1_out, and_2_out, and_3_out, and_4_out);
  or or_4 (or_4_out, and_5_out, and_6_out, and_7_out, and_8_out);
  ExactlyOne xor_3 (.out(xor_3_out), .in1(or_3_out), .in2(A[3]), .in3(B[3]));
  and and_9 (and_9_out, or_3_out, A[3], B[3]);
  and and_10 (and_10_out, or_3_out, A[3]);
  and and_11 (and_11_out, or_3_out, B[3]);
  and and_12 (and_12_out, A[3], B[3]);
  ExactlyOne xor_4 (.out(xor_4_out), .in1(or_4_out), .in2(A[1]), .in3(B[1]));
  and and_13 (and_13_out, or_4_out, A[1], B[1]);
  and and_14 (and_14_out, or_4_out, A[1]);
  and and_15 (and_15_out, or_4_out, B[1]);
  and and_16 (and_16_out, A[1], B[1]);
  or or_5 (S[3], xor_3_out, and_9_out);
  Hex_Digit_Display hex_digit_display_1 (.value(S));  // open: dp
  or or_6 (Cout, and_9_out, and_10_out, and_11_out, and_12_out);
  or or_7 (S[1], xor_4_out, and_13_out);
  or or_8 (or_8_out, and_13_out, and_14_out, and_15_out, and_16_out);
endmodule

module comparador_cero (
  input  [3:0] A,
  output Z
);

  nor nor_1 (Z, A[0], A[1], A[2], A[3]);
endmodule

module sumador_flags (
  input  Cin,
  input  [3:0] A,
  input  [3:0] B,
  output [3:0] S,
  output N,
  output Z,
  output V,
  output C
);

  wire and_1_out, and_2_out, nor_1_out, not_1_out;

  sumador_4_bis sumador_4_bis_1 (.B(A), .B_2(A), .Cin(Cin), .S({N, S[2:0]}), .Cout(C));
  nor nor_1 (nor_1_out, A[3], A[3]);
  comparador_cero comparador_cero_1 (.A({N, S[2:0]}), .Z(Z));
  not not_1 (not_1_out, N);
  and and_1 (and_1_out, N, nor_1_out);
  and and_2 (and_2_out, A[3], not_1_out, A[3]);
  or or_1 (V, and_1_out, and_2_out);
  Hex_Digit_Display hex_digit_display_1 (.value({N, S[2:0]}));  // open: dp

  assign B = A;
  assign S[3] = N;
endmodule

module incrementador_4 (
  input  [3:0] A,
  output [3:0] S
);

  wire sumador_simple_1_cout, sumador_simple_2_cout;

  sumador_simple sumador_simple_1 (.a(A[0]), .b(A[1]), .S(S[1]), .Cout(sumador_simple_1_cout));
  not not_1 (S[0], A[0]);
  sumador_simple sumador_simple_2 (.a(sumador_simple_1_cout), .b(A[2]), .S(S[2]), .Cout(sumador_simple_2_cout));
  sumador_simple sumador_simple_3 (.a(sumador_simple_2_cout), .b(A[3]), .S(S[3]));  // open: Cout
  Hex_Digit_Display hex_digit_display_1 (.value(S));  // open: dp
endmodule

module inversor_4 (
  input  [3:0] A,
  input  INV,
  output [3:0] S
);

  wire [3:0] incrementador_4_1_s, not_1_out;

  not not_1 (not_1_out[0], A[0]);
  Multiplexer #(.width(4)) multiplexer_1 (.in0(A), .in1(incrementador_4_1_s), .out(S), .sel(INV));  // open: en
  not not_2 (not_1_out[1], A[1]);
  not not_3 (not_1_out[2], A[2]);
  not not_4 (not_1_out[3], A[3]);
  Hex_Digit_Display hex_digit_display_1 (.value(S));  // open: dp
  incrementador_4 incrementador_4_1 (.A(not_1_out), .S(incrementador_4_1_s));
endmodule

module ALU (
  input  A,
  input  [3:0] A_2,
  input  A_3,
  input  A_4,
  input  [3:0] B,
  input  [1:0] OP,
  output N,
  output Z,
  output V,
  output C,
  output [3:0] S
);

  wire and_5_out, and_6_out, and_7_out, and_8_out, and_9_out, not_1_out, not_2_out, not_3_out, not_4_out,
       not_5_out, or_6_out, sumador_4_bis_1_cout, xor_1_out;
  wire [3:0] and_1_out, inversor_4_1_s, multiplexer_1_out, multiplexer_2_out, or_1_out, sumador_4_bis_1_s,
       sumador_4_bis_2_s;

  and and_1 (and_1_out[0], A_2[0], B[0]);
  inversor_4 inversor_4_1 (.A(B), .INV(A_4), .S(inversor_4_1_s));
  and and_2 (and_1_out[1], A_2[1], B[1]);
  and and_3 (and_1_out[2], A_2[2], B[2]);
  and and_4 (and_1_out[3], A_2[3], B[3]);
  or or_1 (or_1_out[0], A_2[0], B[0]);
  or or_2 (or_1_out[1], A_2[1], B[1]);
  or or_3 (or_1_out[2], A_2[2], B[2]);
  or or_4 (or_1_out[3], A_2[3], B[3]);
  sumador_4_bis sumador_4_bis_1 (.B(A_2), .B_2(B), .Cin(A_3), .S(sumador_4_bis_1_s), .Cout(sumador_4_bis_1_cout));
  sumador_4_bis sumador_4_bis_2 (.B(A_2), .B_2(inversor_4_1_s), .Cin(A_3), .S(sumador_4_bis_2_s));  // open: Cout
  Multiplexer #(.width(4)) multiplexer_1 (
    .in0(or_1_out), .in1(and_1_out), .out(multiplexer_1_out), .sel(xor_1_out));  // open: en
  Multiplexer #(.width(4)) multiplexer_2 (
    .in0(sumador_4_bis_1_s), .in1(sumador_4_bis_2_s), .out(multiplexer_2_out), .sel(xor_1_out));  // open: en
  xor xor_1 (xor_1_out, OP[0], OP[1]);
  Hay_Overflow hay_overflow_1 (.A(B), .b(A_2), .Cin(A), .Cout(V));  // open: S
  Multiplexer #(.width(4)) multiplexer_3 (
    .in0(multiplexer_2_out), .in1(multiplexer_1_out), .out({N, S[2:0]}), .sel(OP[1]));  // open: en
  not not_1 (not_1_out, A_2[0]);
  not not_2 (not_2_out, A_2[1]);
  not not_3 (not_3_out, A_2[2]);
  comparador_cero comparador_cero_1 (.A({N, S[2:0]}), .Z(Z));
  and and_5 (and_5_out, not_1_out, B[0]);
  and and_6 (and_6_out, not_2_out, B[1]);
  and and_7 (and_7_out, not_3_out, B[2]);
  not not_4 (not_4_out, A_2[3]);
  and and_8 (and_8_out, not_4_out, B[3]);
  or or_5 (C, sumador_4_bis_1_cout, and_9_out);
  or or_6 (or_6_out, and_5_out, and_6_out, and_7_out, and_8_out);
  Hex_Digit_Display hex_digit_display_1 (.value({N, S[2:0]}));  // open: dp
  and and_9 (and_9_out, or_6_out, OP[0], not_5_out);
  not not_5 (not_5_out, OP[1]);

  assign S[3] = N;
endmodule

module Hay_Overflow (
  input  Cin,
  input  [3:0] A,
  input  [3:0] b,
  output Cout,
  output S
);

  wire and_1_out, and_2_out, nor_1_out, not_1_out;
  wire [3:0] sumador_4_bis_1_s;

  sumador_4_bis sumador_4_bis_1 (.B(A), .B_2(A), .Cin(Cin), .S(sumador_4_bis_1_s), .Cout(Cout));
  nor nor_1 (nor_1_out, A[3], A[3]);
  not not_1 (not_1_out, sumador_4_bis_1_s[3]);
  and and_1 (and_1_out, sumador_4_bis_1_s[3], nor_1_out);
  and and_2 (and_2_out, A[3], not_1_out, A[3]);
  or or_1 (S, and_1_out, and_2_out);

  assign b = A;
endmodule

module sumador_4_bis (
  input  Cin,
  input  [3:0] B,
  input  [3:0] B_2,
  output [3:0] S,
  output Cout
);

  wire sumador_completo_1_cout, sumador_completo_2_cout, sumador_completo_3_cout;

  sumador_completo sumador_completo_1 (.A(B[0]), .B(B_2[0]), .Cin(Cin), .S(S[0]), .Cout(sumador_completo_1_cout));
  sumador_completo sumador_completo_2 (
    .A(B[1]), .B(B_2[1]), .Cin(sumador_completo_1_cout), .S(S[1]), .Cout(sumador_completo_2_cout));
  sumador_completo sumador_completo_3 (
    .A(B[2]), .B(B_2[2]), .Cin(sumador_completo_2_cout), .S(S[2]), .Cout(sumador_completo_3_cout));
  sumador_completo sumador_completo_4 (.A(B[3]), .B(B_2[3]), .Cin(sumador_completo_3_cout), .S(S[3]), .Cout(Cout));
  Hex_Digit_Display hex_digit_display_1 (.value(S));  // open: dp
endmodule
